# Fritzing sketch ShutterGlasses (saved by Fritzing 0.3.16b)
breadboards: 1

parts:
  Arduino1 = Arduino
  U1 = LM 358 Dual Op-Amp [package="DIP8 [THT]"]
  U2 = LM 358 Dual Op-Amp [package="DIP8 [THT]"]
  R1 = Resistor [resistance=15k package=THT]
  R2 = Resistor [resistance=15k package=THT]
  R3 = Resistor [resistance=15k package=THT]
  R4 = Resistor [resistance=15k package=THT]
  J1 = screw terminal, 3 pins

nets:
  N1: Arduino1.GND, U1.connector3, U2.connector3, R2.Pin_1, R4.Pin_1, J1.pin1
  N2: Arduino1.D4, U1.connector5, U2.connector4, R3.Pin_0
  N3: Arduino1.+5V, R1.Pin_1, R3.Pin_1
  N4: Arduino1.VIN, U1.connector7, U2.connector7
  N5: U1.connector4, U2.connector5, R1.Pin_0, R2.Pin_0
  N6: U1.connector6, R4.Pin_0, J1.pin2
  N7: U2.connector6, J1.pin3
